# Fritzing sketch RotaryEncoderWithButton (saved by Fritzing 0.9.3b)
breadboards: 1

parts:
  Meadow1 = Meadow F7
  LED1 = LED - 5mm [color="Red (633nm)" package="5 mm [THT]"]

nets:
  N1: Meadow1.GND, LED1.cathode
  N2: Meadow1.D12, LED1.anode

custom parts:
  Meadow F7: A prototyping board running full .Net Standard 2.X
